# Fritzing sketch led_button_schema (saved by Fritzing 0.9.3b)
circuit board: 8.46667cm x 5.64444cm
breadboards: 1

parts:
  Part1 = Arduino Uno (Rev3)
  S1 = Pushbutton [package="[THT]"]
  LED1 = LED - 5mm [color="Yellow (595nm)" package="5 mm [THT]"]
  R2 = Resistor [tolerance=±5% resistance=220 package=THT]
  R1 = Resistor [tolerance=±5% resistance=10k package=THT]

nets:
  N1: Part1.D2, R2.Pin_1
  N2: Part1.5V, S1.Pin_3, S1.Pin_4
  N3: Part1.GND, LED1.cathode, R1.Pin_1
  N4: S1.Pin_1, S1.Pin_2, R1.Pin_0
  N5: LED1.anode, R2.Pin_0
