# Fritzing sketch leds_red_yellow_button_schema (saved by Fritzing 0.9.3b)
circuit board: 8.46667cm x 5.64444cm
breadboards: 1

parts:
  Part1 = Arduino Uno (Rev3)
  S1 = Pushbutton [package="[THT]"]
  LED1 = LED - 5mm [color="Yellow (595nm)" package="5 mm [THT]"]
  R2 = Resistor [tolerance=±5% resistance=220 package=THT]
  LED2 = LED - 5mm [color="Red (633nm)" package="5 mm [THT]"]
  R3 = Resistor [tolerance=±5% resistance=220 package=THT]
  R4 = Resistor [tolerance=±5% resistance=10k package=THT]

nets:
  N1: Part1.D2, R2.Pin_1
  N2: Part1.D7, R3.Pin_1
  N3: Part1.5V, S1.Pin_3, S1.Pin_4
  N4: Part1.GND, LED1.cathode, LED2.cathode, R4.Pin_1
  N5: S1.Pin_1, S1.Pin_2, R4.Pin_0
  N6: LED1.anode, R2.Pin_0
  N7: LED2.anode, R3.Pin_0
