# Fritzing sketch photoresistor_led_schema (saved by Fritzing 0.9.3b)
circuit board: 8.72414cm x 7.72632cm
breadboards: 1

parts:
  Part1 = Arduino Uno (Rev3)
  S1 = Pushbutton [package="[THT]"]
  DI1 = 7-Segment LED Display [package=THT]
  R3 = Resistor [tolerance=±5% resistance=220 package=THT]
  R4 = Resistor [tolerance=±5% resistance=220 package=THT]
  R5 = Resistor [tolerance=±5% resistance=220 package=THT]
  R6 = Resistor [tolerance=±5% resistance=220 package=THT]
  R7 = Resistor [tolerance=±5% resistance=220 package=THT]
  R8 = Resistor [tolerance=±5% resistance=220 package=THT]
  R9 = Resistor [tolerance=±5% resistance=220 package=THT]
  R10 = Resistor [tolerance=±5% resistance=10k package=THT]

nets:
  N1: Part1.D8, R9.Pin_1
  N2: Part1.D9_PWM, R7.Pin_0
  N3: Part1.D10_PWM/SS, R8.Pin_0
  N4: Part1.GND, R10.Pin_1
  N5: Part1.D3_PWM, S1.Pin_1, S1.Pin_2, R10.Pin_0
  N6: Part1.D4, R4.Pin_1
  N7: Part1.D5_PWM, R5.Pin_0
  N8: Part1.D6_PWM, R6.Pin_0
  N9: Part1.D7, R3.Pin_1
  N10: Part1.5V, S1.Pin_3, S1.Pin_4, DI1.commAnode
  N11: DI1.cathodeE, R7.Pin_1
  N12: DI1.cathodeD, R8.Pin_1
  N13: DI1.cathodeC, R9.Pin_0
  N14: DI1.cathodeB, R3.Pin_0
  N15: DI1.cathodeA, R4.Pin_0
  N16: DI1.cathodeF, R5.Pin_1
  N17: DI1.cathodeG, R6.Pin_1
